// Logisim project control-logic.circ as structural Verilog: 1 circuit, main circuit control_logic
module control_logic (
  input  [31:0] Instruction,
  input  BrEq,
  input  BrLt,
  output PCSel,
  output RegWEn,
  output [2:0] ImmSel,
  output BrUn,
  output ASel,
  output BSel,
  output [3:0] ALUSel,
  output MemWEn,
  output [1:0] WBSel
);

  wire and_2_out, and_3_out, and_8_out, funct3_01_00, funct3_01_01, funct3_01_11, funct3_2_0, funct3_2_1,
       funct7_45_00, funct7_45_01, is_add, is_addi, is_and, is_andi, is_auipc, is_beq, is_bge, is_bgeu,
       is_blt, is_bltu, is_bne, is_Btype, is_jal, is_jalr, is_lb, is_lh, is_lui, is_lw, is_mul, is_mulh,
       is_mulhu, is_or, is_ori, is_Rtype, is_sb, is_sh, is_sll, is_slli, is_slt, is_slti, is_sra, is_srai,
       is_srl, is_srli, is_Stype, is_sub, is_sw, is_Utype, is_xor, is_xori, not_1_out, not_2_out, not_3_out,
       opcode_6_0, opcode_6_1, opcode_23_00, opcode_23_01, opcode_45_00, opcode_45_01, opcode_45_10,
       opcode_45_11, Rtype_funct3_000;
  wire [1:0] funct3_01;
  wire [2:0] opcode23;
  wire [5:0] priority_encoder_1_out;
  wire [15:14] rom_1_data;

  and and_1 (is_Rtype, opcode_45_11, opcode_23_00);
  and and_2 (and_2_out, opcode_23_00, opcode_45_10);
  and and_3 (and_3_out, is_Rtype, funct3_01_00);
  and and_4 (Rtype_funct3_000, and_3_out, funct3_2_0);
  not not_1 (not_1_out, funct3_2_0);
  and and_5 (is_Stype, and_2_out, opcode_6_0);
  not not_2 (not_2_out, opcode_6_0);
  and and_6 (is_Btype, and_2_out, not_2_out);
  Comparator #(.width(3)) comparator_1 (.a(opcode23), .b(3'b001), .gt(is_jal), .eq(opcode_23_01), .lt(opcode_23_00));
  Comparator #(.width(2)) comparator_2 (
    .a(Instruction[5:4]), .b(2'b10), .gt(opcode_45_11), .eq(opcode_45_10));  // open: lt
  Comparator #(.width(2)) comparator_3 (
    .a(Instruction[5:4]), .b(2'b01), .eq(opcode_45_01), .lt(opcode_45_00));  // open: gt
  Comparator #(.width(1)) comparator_4 (.a(Instruction[6]), .b(1'b1), .eq(opcode_6_1), .lt(opcode_6_0));  // open: gt
  and and_7 (is_xor, and_3_out, not_1_out);
  and and_8 (and_8_out, opcode_23_01, opcode_45_11);
  Priority_Encoder #(.select_enc(6)) priority_encoder_1 (
    .in0(is_add), .in1(is_mul), .in2(is_sub), .in3(is_sll), .in4(is_mulh), .in5(is_mulhu), .in6(is_slt),
    .in7(is_xor), .in8(is_srl), .in9(is_sra), .in10(is_or), .in11(is_and), .in12(is_lb), .in13(is_lh),
    .in14(is_lw), .in15(is_addi), .in16(is_slli), .in17(is_slti), .in18(is_xori), .in19(is_srli),
    .in20(is_srai), .in21(is_ori), .in22(is_andi), .in23(is_sb), .in24(is_sh), .in25(is_sw), .in26(is_beq),
    .in27(is_bne), .in28(is_blt), .in29(is_bge), .in30(is_bltu), .in31(is_bgeu), .in32(is_auipc),
    .in33(is_lui), .in34(is_jal), .in35(is_jalr), .out(priority_encoder_1_out));  // open: in36, in37, in38, in39, in40, in41, in42, in43, in44, in45, in46, in47, in48, in49, in50, in51, in52, in53, in54, in55, in56, in57, in58, in59, in60, in61, in62, in63, gs, en_out, en_in
  and and_9 (is_Utype, and_8_out, opcode_6_0);
  ROM #(.addrWidth(6), .dataWidth(16)) rom_1 (
    .addr(priority_encoder_1_out),
    .data({rom_1_data, WBSel, MemWEn, ALUSel, BSel, ASel, BrUn, ImmSel, RegWEn}));
  Comparator #(.width(2)) comparator_5 (.a(funct3_01), .b(2'b10), .gt(funct3_01_11), .eq(opcode_45_10));  // open: lt
  Comparator #(.width(2)) comparator_6 (.a(funct3_01), .b(2'b01), .eq(funct3_01_01), .lt(funct3_01_00));  // open: gt
  Comparator #(.width(1)) comparator_7 (.a(Instruction[14]), .b(1'b1), .eq(funct3_2_1), .lt(funct3_2_0));  // open: gt
  Comparator #(.width(2)) comparator_8 (
    .a(Instruction[30:29]), .b(2'b01), .eq(funct7_45_01), .lt(funct7_45_00));  // open: gt
  not not_3 (not_3_out, funct7_45_00);
  buf and_10 (is_sub, not_3_out);  // AND_Gate

  // Other names for the same wires on the sheet: opcode_01[1:0] = Instruction[1:0]; opcode_23[1:0] = Instruction[3:2];
  //   opcode_45[1:0] = Instruction[5:4]; opcode_6 = Instruction[6]; rd_imm[4:0] = Instruction[11:7];
  //   fuct3_01[1:0] = Instruction[13:12]; funct3_2 = Instruction[14]; rs_imm[9:0] = Instruction[24:15];
  //   funct7_01[1:0] = Instruction[26:25]; funct7_23[1:0] = Instruction[28:27]; funct7_45[1:0] = Instruction[30:29];
  //   funct7_6 = Instruction[31]

  // Notes on the sheet:
  //   INPUTS to your circuit
  //   DON'T CHANGE THE LOCATIONS OF THE INPUTS AND OUTPUTS!
  //   Connect ROM Input here ->
  //   OUTPUT from your circuit
  //   contents of rom_1 (hex, n*v repeats v):
  //   102b 142b 162b 10ab 14ab 15ab 112b 122b 12ab 16ab 132b 13ab 61 61 61 1061 10e1 1161 1261 12e1 16e1
  //   1361 13e1 862 862 862 4*44 54 44 1047 17e7 2049 2061
  //   ROM FOR CONTROL LOGIC
  //   This is only if you choose to do the ROM option
  //   CONNECT
  //   WIRE
  //   TO
  //   USE
  //   ROM
  //   Reminder: If using ROM, use combinational logic for PCSel
endmodule
